# Fritzing sketch cheTempoFa-0.1 (saved by Fritzing 0.9.3b)
circuit board: 4.29609cm x 4.89654cm
breadboards: 1

parts:
  U1 = ESP8266 WiFi Module [part_number=ESP8266]
  R1 = Resistor [tolerance=±5% resistance=3.3k package=THT]
  R2 = Resistor [tolerance=±5% resistance=3.3k package=THT]
  R3 = Resistor [tolerance=±5% resistance=3.3k package=THT]
  R4 = Resistor [tolerance=±5% resistance=3.3k package=THT]
  R5 = Resistor [tolerance=±5% resistance=330 package=THT]
  R6 = Resistor [tolerance=±5% resistance=330 package=THT]
  OLED1 = OLED 128x64 I2C Monochrome Display
  HLK-PM1 = HLK-PM01
  JP1 = Header 2 [package=screwterminal-3.5mm-2_lock]
  J1_USB_adapter = male pin header, 6 pins [form="♂ (male)"]
  S1_Function = Momentary Switch [package=ksa_sealed_tac_switch]
  S2_Reset = Momentary Switch [package=ksa_sealed_tac_switch]
  J2_GPIO_0_program = male pin header, 2 pins [form="♂ (male)"]
  C1 = Electrolytic Capacitor [capacitance=100nF package="100 mil [THT, electrolytic]"]

nets:
  N1: U1.RXD, J1_USB_adapter.pin4, S1_Function.3, S1_Function.4
  VCC: U1.VCC, R1.Pin_1, R2.Pin_1, R3.Pin_1, R4.Pin_1, OLED1.VDD, HLK-PM1.+Vo, J1_USB_adapter.pin3, C1.+
  N2: U1.GPIO_0, R1.Pin_0, R5.Pin_1, J2_GPIO_0_program.pin2
  N3: U1.GPIO_16, R3.Pin_0, S2_Reset.3, S2_Reset.4
  N4: U1.GPIO_2, R2.Pin_0, R6.Pin_1
  N5: U1.CH_PD, R4.Pin_0
  GND: U1.GND, OLED1.GND, HLK-PM1.-Vo, J1_USB_adapter.pin1, S1_Function.1, S1_Function.2, S2_Reset.1, S2_Reset.2, J2_GPIO_0_program.pin1, C1.-
  N6: U1.TXD, J1_USB_adapter.pin5
  N7: R5.Pin_0, OLED1.SDA
  N8: R6.Pin_0, OLED1.SCK
  N9: HLK-PM1.AC#0, JP1.2
  N10: HLK-PM1.AC#1, JP1.1

notes:
  Vcc
  GND
  220V AC
  GND - nc - Vcc - TX - RX - nc
  GPIO_0 close to program
  cheTempoFa
  https://github.com/matteomarchesi/cheTempoFa
  2019 - Open Source & Open Hardware

custom parts:
  ESP8266 WiFi Module: Generic WiFi Module based on the ESP8266 with onboard PCB antenna and UART communications
  HLK-PM01: AC-DC 220V to 5V Step-Down Power Supply Module
