# Fritzing sketch cheTempoFa (saved by Fritzing 0.9.3b)
circuit board: 8.46667cm x 5.64444cm
breadboards: 1

parts:
  S1_funct = Pushbutton [package="[THT]"]
  U1 = ESP8266 WiFi Module [part_number=ESP8266]
  R1 = Resistor [tolerance=±5% resistance=3.3k package=THT]
  R2 = Resistor [tolerance=±5% resistance=3.3k package=THT]
  R3 = Resistor [tolerance=±5% resistance=3.3k package=THT]
  R4 = Resistor [tolerance=±5% resistance=3.3k package=THT]
  J1_AC_220V = female pin header, 2 pins [form="♀ (female)"]
  J2_USB_adaptor = female pin header, 6 pins [form="♀ (female)"]
  J3_program = female pin header, 2 pins [form="♀ (female)"]
  R5 = Resistor [tolerance=±5% resistance=330 package=THT]
  R6 = Resistor [tolerance=±5% resistance=330 package=THT]
  S2_reset = Pushbutton [package="[THT]"]
  HLK-PM1 = HLK-PM01
  I2C_OLED = female alternating pin header, 4 pins [form="♀ (female)"]

nets:
  GND: S1_funct.Pin_1, S1_funct.Pin_2, U1.GND, J2_USB_adaptor.pin1, J3_program.pin2, S2_reset.Pin_1, S2_reset.Pin_2, HLK-PM1.-Vo, I2C_OLED.pin1
  N1: S1_funct.Pin_3, S1_funct.Pin_4, U1.RXD, R5.Pin_0
  N2: U1.VCC, R1.Pin_1, R2.Pin_1, R3.Pin_1, R4.Pin_1, J2_USB_adaptor.pin3, HLK-PM1.+Vo, I2C_OLED.pin2
  N3: U1.GPIO_0, R2.Pin_0, J3_program.pin1, I2C_OLED.pin4
  N4: U1.GPIO_16, R1.Pin_0, S2_reset.Pin_3, S2_reset.Pin_4
  N5: U1.GPIO_2, R4.Pin_0, I2C_OLED.pin3
  N6: U1.CH_PD, R3.Pin_0
  N7: U1.TXD, R6.Pin_0
  N8: J1_AC_220V.pin1, HLK-PM1.AC#1
  N9: J1_AC_220V.pin2, HLK-PM1.AC#0
  N10: J2_USB_adaptor.pin4, R5.Pin_1
  N11: J2_USB_adaptor.pin5, R6.Pin_1

notes:
  AC 220V

custom parts:
  ESP8266 WiFi Module: Generic WiFi Module based on the ESP8266 with onboard PCB antenna and UART communications
  HLK-PM01: AC-DC 220V to 5V Step-Down Power Supply Module
